# Fritzing sketch Koblingsskjema (saved by Fritzing 0.9.3b)
breadboards: 1

parts:
  Part1 = Arduino Uno (Rev3) - ICSP
  Part2 = Bluetooth HC-05 Macho
  hc-sr1 = hc-sr04
  LED1 = LED - 5mm [color="Red (633nm)" package="5 mm [THT]"]
  R1 = Resistor [tolerance=±20% resistance=220 package="2512 [SMD]"]

nets:
  N1: Part1.A1, Part2.TXD
  N2: Part1.A4/SDA, Part2.RXD
  N3: Part1.D2, hc-sr1.Trig
  N4: Part1.D3_PWM, hc-sr1.Echo
  N5: Part1.D6_PWM, LED1.anode
  VCC: Part1.5V, Part2.VCC, hc-sr1.VCC
  GND: Part1.GND, Part2.GND, hc-sr1.GND, R1.Pin_0
  N6: LED1.cathode, R1.Pin_1
